# Fritzing sketch Diagrama_tcc_fr (saved by Fritzing 1.0.6)

parts:
  A1 = DFR SEN0240
  Componente1 = 16-Channel 12-bit PWM Servo Driver - I2C [part_number=815]
  J1 = Basic Servo
  J2 = Basic Servo
  J3 = Basic Servo
  J4 = Basic Servo
  S1 = SWITCH-MOMENTARY-2 [package=tactile-switch-1101ne]
  S2 = SWITCH-MOMENTARY-2 [package=tactile-switch-1101ne]
  S3 = SWITCH-MOMENTARY-2 [package=tactile-switch-1101ne]
  S4 = SWITCH-MOMENTARY-2 [package=tactile-switch-1101ne]
  U1 = LIPO-110mAh [package=lipo-110]
  OLED_I2C1 = OLED 128x64 I2C Monochrome Display
  A2 = Esp32-c3 super mini
  Q2 = PNP-Transistor [part_number=3144 package="SOT-23 [SMD]"]
  Q3 = PNP-Transistor [part_number=3144 package="SOT-23 [SMD]"]
  Q4 = PNP-Transistor [part_number=3144 package="SOT-23 [SMD]"]
  Q5 = PNP-Transistor [part_number=3144 package="SOT-23 [SMD]"]
  J5 = Basic Servo
  C1 = Capacitor Polarized [package=panasonic_e]
  A4 = USB power module
  M1 = Dagu DGServo 9g (Pan and tilt) [part_number=RS001B]
  Q6 = PNP-Transistor [part_number=3144 package="SOT-23 [SMD]"]
  M2 = DOIT Esp32 DevKit v1 (30 pins long, 11 pins width) [part_number=ESP32S-PIN30]

nets:
  N1: A1.Pin_1, M2.D34
  N2: A1.Pin_3, S1.2, S2.2, S3.2, S4.2, C1.-, M2.GND
  N3: Componente1.PWRIN, A2.Pin_16, A4.Pin_1, A4.Pin_2, Q6.2
  N4: Componente1.GND, A2.Pin_15, A4.Pin_4, A4.Pin_5, A4.Pin_6, Q6.0
  N5: Componente1.PWM4, J2.pulse
  N6: Componente1.PWM3, J4.pulse
  N7: Componente1.PWM2, J5.pulse
  N8: Componente1.PWM1, J1.pulse
  N9: Componente1.PWM0, J3.pulse
  N10: Componente1.VCC, A2.Pin_14
  N11: Componente1.SDA, A2.Pin_4
  N12: Componente1.SCL, A2.Pin_5
  N13: Componente1.PWM8, M1.pulse
  N14: S1.1, M2.D23
  N15: S2.1, M2.D18
  N16: S3.1, M2.D2
  N17: S4.1, M2.D15
  N18: U1.-, OLED_I2C1.GND
  N19: OLED_I2C1.SDA, M2.D21
  N20: OLED_I2C1.SCK, M2.D22
  N21: A2.Pin_9, Q6.1
  N22: A2.Pin_10, Q5.1
  N23: A2.Pin_11, Q2.1
  N24: A2.Pin_12, Q3.1
  N25: A2.Pin_13, Q4.1
  N26: C1.+, M2.VIN

custom parts:
  DFR SEN0240: This EMG sensor is launched by the cooperation of DFRobot and OYMotion, which can detect sEMG to reflect muscle and neural activities of human.
  16-Channel 12-bit PWM Servo Driver - I2C: You want to make a cool robot, maybe a hexapod walker, or maybe just a piece of art with a lot of moving parts. Or maybe you want to drive a lot of LEDs with precise PWM output. Using only two pins, control 16 free-running PWM outputs! You can even chain up 62 breakouts to control up to 992 PWM outputs.
  Esp32-c3 super mini: ESP32-C3 Development Board ESP32 SuperMini Development Board ESP32 Development Board WiFi Bluetooth.
  USB power module: PD QC AFC Fast Charge Decoy Trigger Module USB-PWR Module Supports 5V 9V 12V 15V 20V Fixed Voltage Output.
  DOIT Esp32 DevKit v1 (30 pins long, 11 pins width): The DOIT Esp32 DevKit v1 is one of the development board created by DOIT to evaluate the ESP-WROOM-32 module. It is based on the ESP32 microcontroller that boasts Wifi, Bluetooth, Ethernet and Low Power support all in a single chip. (vanepp) made breadboard work, adjusted pin numbering and labels and reduced size of schematic and cleaned up pcb. This chip is 30pins long (2 x15) and 11 pins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
